# Fritzing sketch sketch (saved by Fritzing 0.9.4)

parts:
  Raspberry_Pi1 = Raspberry Pi B rev2
  WeMos_D1_Mini_Relay_Shield_V1 = WeMos D1 Mini Relay Shield V2

nets:
  3V3: Raspberry_Pi1.3V3, WeMos_D1_Mini_Relay_Shield_V1.3V3
  N1: Raspberry_Pi1.GND, WeMos_D1_Mini_Relay_Shield_V1.G
  N2: Raspberry_Pi1.GPIO_18, WeMos_D1_Mini_Relay_Shield_V1.D1
